// Logisim project s5.circ as structural Verilog: 1 circuit, main circuit main
module main (
  input  A,
  input  B,
  input  C,
  output out_4,
  output out_5
);

  wire and_1_out, and_2_out, and_3_out, and_4_out, and_5_out, and_6_out, and_7_out, and_8_out, and_9_out,
       not_1_out, not_2_out, not_3_out, not_4_out, not_5_out, not_6_out, not_7_out, not_8_out, not_9_out,
       not_10_out, not_11_out, not_12_out, not_13_out;

  not not_1 (not_1_out, A);
  not not_2 (not_2_out, B);
  not not_3 (not_3_out, C);
  not not_4 (not_4_out, A);
  not not_5 (not_5_out, C);
  not not_6 (not_6_out, A);
  not not_7 (not_7_out, B);
  not not_8 (not_8_out, C);
  not not_9 (not_9_out, B);
  not not_10 (not_10_out, C);
  not not_11 (not_11_out, A);
  not not_12 (not_12_out, C);
  not not_13 (not_13_out, A);
  and and_1 (and_1_out, not_1_out, not_2_out, not_3_out);
  and and_2 (and_2_out, not_4_out, B, not_5_out);
  and and_3 (and_3_out, not_6_out, B, C);
  and and_4 (and_4_out, A, not_7_out, C);
  and and_5 (and_5_out, A, B, not_8_out);
  and and_6 (and_6_out, A, not_9_out, C);
  and and_7 (and_7_out, B, not_10_out);
  and and_8 (and_8_out, not_11_out, not_12_out);
  and and_9 (and_9_out, not_13_out, B);
  or or_1 (out_4, and_1_out, and_2_out, and_3_out, and_4_out, and_5_out);
  or or_2 (out_5, and_6_out, and_7_out, and_8_out, and_9_out);
endmodule
